// Logisim project TallerLogica-Combinatorios.circ as structural Verilog: 9 circuits, main circuit verificador
module sumador_simple (
  input  A,
  input  B,
  output S,
  output Cout
);

  xor xor_1 (S, A, B);
  and and_1 (Cout, A, B);
endmodule

module sumador_completo (
  input  A,
  input  B,
  input  Cin,
  output S,
  output Cout
);

  wire sumador_simple_1_cout, sumador_simple_1_s, sumador_simple_2_cout;

  sumador_simple sumador_simple_1 (.A(A), .B(B), .S(sumador_simple_1_s), .Cout(sumador_simple_1_cout));
  sumador_simple sumador_simple_2 (.A(sumador_simple_1_s), .B(Cin), .S(S), .Cout(sumador_simple_2_cout));
  or or_1 (Cout, sumador_simple_2_cout, sumador_simple_1_cout);
endmodule

module sumador_4 (
  input  Cin,
  input  [3:0] A,
  input  [3:0] B,
  output [3:0] S,
  output Cout
);

  wire sumador_completo_1_cout, sumador_completo_2_cout, sumador_completo_3_cout;

  sumador_completo sumador_completo_1 (.A(A[0]), .B(B[0]), .Cin(Cin), .S(S[0]), .Cout(sumador_completo_1_cout));
  sumador_completo sumador_completo_2 (
    .A(A[1]), .B(B[1]), .Cin(sumador_completo_1_cout), .S(S[1]), .Cout(sumador_completo_2_cout));
  sumador_completo sumador_completo_3 (
    .A(A[2]), .B(B[2]), .Cin(sumador_completo_2_cout), .S(S[2]), .Cout(sumador_completo_3_cout));
  Hex_Digit_Display hex_digit_display_1 (.value(S));  // open: dp
  sumador_completo sumador_completo_4 (.A(A[3]), .B(B[3]), .Cin(sumador_completo_3_cout), .S(S[3]), .Cout(Cout));
endmodule

module comparador_cero (
  input  [3:0] A,
  output Z
);

  wire or_1_out, or_2_out, or_3_out;

  or or_1 (or_1_out, A[0], A[1]);
  or or_2 (or_2_out, A[2], A[3]);
  or or_3 (or_3_out, or_1_out, or_2_out);
  not not_1 (Z, or_3_out);
endmodule

module sumador_flags (
  input  Cin,
  input  [3:0] A,
  input  [3:0] B,
  output [3:0] S,
  output Z,
  output N,
  output C,
  output V
);

  wire not_1_out, sumador_completo_1_cout, sumador_completo_2_cout, sumador_completo_3_cout, xor_1_out,
       xor_2_out;

  sumador_completo sumador_completo_1 (.A(A[0]), .B(B[0]), .Cin(Cin), .S(S[0]), .Cout(sumador_completo_1_cout));
  xor xor_1 (xor_1_out, A[3], B[3]);
  not not_1 (not_1_out, xor_1_out);
  xor xor_2 (xor_2_out, B[3], sumador_completo_3_cout);
  sumador_completo sumador_completo_2 (
    .A(A[1]), .B(B[1]), .Cin(sumador_completo_1_cout), .S(S[1]), .Cout(sumador_completo_2_cout));
  and and_1 (V, not_1_out, xor_2_out);
  sumador_completo sumador_completo_3 (
    .A(A[2]), .B(B[2]), .Cin(sumador_completo_2_cout), .S(S[2]), .Cout(sumador_completo_3_cout));
  Hex_Digit_Display hex_digit_display_1 (.value({N, S[2:0]}));  // open: dp
  sumador_completo sumador_completo_4 (.A(A[3]), .B(B[3]), .Cin(sumador_completo_3_cout), .S(N), .Cout(C));
  comparador_cero comparador_cero_1 (.A({N, S[2:0]}), .Z(Z));

  assign S[3] = N;
endmodule

module incrementador_4 (
  input  [3:0] A,
  output [3:0] S
);

  Hex_Digit_Display hex_digit_display_1 (.value(S));  // open: dp
  sumador_4 sumador_4_1 (.A(A), .B(4'b0001), .S(S));  // open: Cin, Cout
endmodule

module inversor_4 (
  input  [3:0] A,
  input  INV,
  output [3:0] S
);

  wire [3:0] incrementador_4_1_s, not_1_out;

  not not_1 (not_1_out[0], A[0]);
  not not_2 (not_1_out[1], A[1]);
  not not_3 (not_1_out[2], A[2]);
  not not_4 (not_1_out[3], A[3]);
  incrementador_4 incrementador_4_1 (.A(not_1_out), .S(incrementador_4_1_s));
  Multiplexer #(.width(4)) multiplexer_1 (.in0(A), .in1(incrementador_4_1_s), .out(S), .sel(INV));
  Hex_Digit_Display hex_digit_display_1 (.value(S));  // open: dp
endmodule

module ALU (
  input  [3:0] A,
  input  [3:0] B,
  input  [1:0] OP,
  output N,
  output Z,
  output V,
  output C,
  output [3:0] S
);

  wire comparador_cero_1_z, comparador_cero_2_z, not_2_out, not_3_out, sumador_flags_2_c, sumador_flags_2_v;
  wire [2:0] and_1_out, or_1_out;
  wire [3:0] comparador_cero_3_z, comparador_cero_4_z, inversor_4_1_s, sumador_flags_1_s, sumador_flags_1_z,
       sumador_flags_2_s, sumador_flags_2_z;
  wire [3:3] not_1_out;

  not not_1 (not_1_out[3], B[3]);
  not not_2 (not_2_out, A[3]);
  inversor_4 inversor_4_1 (.A(B), .S(inversor_4_1_s));  // open: INV
  comparador_cero comparador_cero_1 (.A({not_1_out[3], B[2:0]}), .Z(comparador_cero_1_z));
  comparador_cero comparador_cero_2 (.A(B), .Z(comparador_cero_2_z));
  and and_1 (and_1_out[0], A[0], B[0]);
  and and_2 (comparador_cero_3_z[3], A[1], B[1]);
  and and_3 (and_1_out[2], A[2], B[2]);
  and and_4 (comparador_cero_3_z[3], A[3], B[3]);
  or or_1 (or_1_out[0], A[0], B[0]);
  or or_2 (or_1_out[1], A[1], B[1]);
  or or_3 (or_1_out[2], A[2], B[2]);
  or or_4 (comparador_cero_4_z[3], A[3], B[3]);
  sumador_flags sumador_flags_1 (
    .A(A), .B(B), .S(sumador_flags_1_s), .Z(sumador_flags_1_z[0]), .N(sumador_flags_1_z[3]),
    .C(sumador_flags_1_z[1]), .V(sumador_flags_1_z[2]));  // open: Cin
  Multiplexer multiplexer_1 (.in0(not_3_out), .in1(1'b0), .out(sumador_flags_2_z[1]), .sel(comparador_cero_2_z));
  sumador_flags sumador_flags_2 (
    .A(A), .B(inversor_4_1_s), .S(sumador_flags_2_s), .Z(sumador_flags_2_z[0]), .N(sumador_flags_2_z[3]),
    .C(sumador_flags_2_c), .V(sumador_flags_2_v));  // open: Cin
  not not_3 (not_3_out, sumador_flags_2_c);
  Multiplexer multiplexer_2 (
    .in0(sumador_flags_2_v), .in1(not_2_out), .out(sumador_flags_2_z[2]), .sel(comparador_cero_1_z));
  comparador_cero comparador_cero_3 (
    .A({comparador_cero_3_z[3], and_1_out[2], comparador_cero_3_z[3], and_1_out[0]}),
    .Z(comparador_cero_3_z[0]));
  comparador_cero comparador_cero_4 (.A({comparador_cero_4_z[3], or_1_out}), .Z(comparador_cero_4_z[0]));
  Multiplexer #(.select(2), .width(4)) multiplexer_3 (
    .in0(sumador_flags_1_s), .in1(sumador_flags_2_s),
    .in2({comparador_cero_3_z[3], and_1_out[2], comparador_cero_3_z[3], and_1_out[0]}),
    .in3({comparador_cero_4_z[3], or_1_out}), .out(S), .sel(OP));
  Multiplexer #(.select(2), .width(4)) multiplexer_4 (
    .in0(sumador_flags_1_z), .in1(sumador_flags_2_z),
    .in2({comparador_cero_3_z[3], 2'b00, comparador_cero_3_z[0]}), .in3(comparador_cero_4_z),
    .out({N, V, C, Z}), .sel(OP));
  Hex_Digit_Display hex_digit_display_1 (.value(S));  // open: dp

  // Notes on the sheet:
  //   N
  //   N
endmodule

module verificador (
  output [3:0] out_1,
  output [3:0] out_2,
  output [1:0] out_3,
  output halt,
  output N,
  output Z,
  output V,
  output C,
  output [3:0] res
);

  wire clock_1_out;

  Clock clock_1 (.out(clock_1_out));
  Counter #(.max('h3ff), .width(10)) counter_1 (
    .clk(clock_1_out), .carry(halt), .Q({out_3, out_2, out_1}));  // open: clr, load, up, count, D
  ALU alu_1 (.A(out_1), .B(out_2), .OP(out_3), .N(N), .Z(Z), .V(V), .C(C), .S(res));
endmodule
